# Fritzing sketch DP001-Schaltung (saved by Fritzing 0.8.3b)
breadboards: 1

parts:
  Arduino_Uno = Arduino Uno (Rev3)
  IC1 = ULN2003A [package="DIP16 [THT]"]
  LED2 = Super Flux LED blue [color=Red]
  LED3 = Super Flux LED blue [color=Green]
  LED1 = Super Flux LED blue [color=Blue]

nets:
  N1: Arduino_Uno.ICSP_MISO, Arduino_Uno.D12/MISO, IC1.In_2
  N2: Arduino_Uno.ICSP_SCK, IC1.In_3
  N3: Arduino_Uno.ICSP_MOSI, Arduino_Uno.D11_PWM/MOSI, IC1.In_1
  GND: Arduino_Uno.GND, IC1.0V
  N4: IC1.Out_3, LED3.cathode
  N5: IC1.Out_2, LED2.cathode
  N6: IC1.Out_1, LED1.cathode
  12V: LED2.anode, LED3.anode, LED1.anode
